// Logisim project DIGITAL_CLOCK.circ as structural Verilog: 1 circuit, main circuit main
module main (
  output out_1,
  output out_2,
  output seconds,
  output out_4,
  output out_5,
  output out_6,
  output out_7,
  output out_8,
  output out_9,
  output out_10,
  output out_11,
  output out_12,
  output out_13,
  output out_14,
  output out_15,
  output hours,
  output out_17,
  output out_18
);

  wire and_1_out, and_2_out, and_3_out, clock_1_out, not_1_out, not_2_out, not_3_out, not_4_out, not_5_out,
       not_6_out, not_7_out, not_8_out;

  Clock clock_1 (.out(clock_1_out));
  J_K_Flip_Flop #(.trigger("falling")) j_k_ff_1 (
    .J(1'b1), .clk(clock_1_out), .K(1'b1), .Q(out_6), .en(1'b1), .reset(and_1_out));  // open: Qn, preset
  not not_1 (not_1_out, out_6);
  J_K_Flip_Flop #(.trigger("falling")) j_k_ff_2 (
    .J(1'b1), .clk(out_6), .K(1'b1), .Q(out_5), .en(1'b1), .reset(and_1_out));  // open: Qn, preset
  not not_2 (not_2_out, out_5);
  J_K_Flip_Flop #(.trigger("falling")) j_k_ff_3 (
    .J(1'b1), .clk(and_1_out), .K(1'b1), .Q(out_12), .en(1'b1), .reset(and_2_out));  // open: Qn, preset
  not not_3 (not_3_out, out_12);
  J_K_Flip_Flop #(.trigger("falling")) j_k_ff_4 (
    .J(1'b1), .clk(and_2_out), .K(1'b1), .Q(out_18), .en(1'b1), .reset(and_3_out));  // open: Qn, preset
  not not_4 (not_4_out, out_18);
  J_K_Flip_Flop #(.trigger("falling")) j_k_ff_5 (
    .J(1'b1), .clk(out_5), .K(1'b1), .Q(out_4), .en(1'b1), .reset(and_1_out));  // open: Qn, preset
  J_K_Flip_Flop #(.trigger("falling")) j_k_ff_6 (
    .J(1'b1), .clk(out_12), .K(1'b1), .Q(out_11), .en(1'b1), .reset(and_2_out));  // open: Qn, preset
  not not_5 (not_5_out, out_11);
  J_K_Flip_Flop #(.trigger("falling")) j_k_ff_7 (
    .J(1'b1), .clk(out_18), .K(1'b1), .Q(out_17), .en(1'b1), .reset(and_3_out));  // open: Qn, preset
  not not_6 (not_6_out, out_17);
  J_K_Flip_Flop #(.trigger("falling")) j_k_ff_8 (
    .J(1'b1), .clk(out_4), .K(1'b1), .Q(seconds), .en(1'b1), .reset(and_1_out));  // open: Qn, preset
  and and_1 (and_1_out, not_1_out, not_2_out, out_4, seconds, out_2, out_1);
  J_K_Flip_Flop #(.trigger("falling")) j_k_ff_9 (
    .J(1'b1), .clk(out_11), .K(1'b1), .Q(out_10), .en(1'b1), .reset(and_2_out));  // open: Qn, preset
  J_K_Flip_Flop #(.trigger("falling")) j_k_ff_10 (
    .J(1'b1), .clk(out_17), .K(1'b1), .Q(hours), .en(1'b1), .reset(and_3_out));  // open: Qn, preset
  not not_7 (not_7_out, hours);
  J_K_Flip_Flop #(.trigger("falling")) j_k_ff_11 (
    .J(1'b1), .clk(seconds), .K(1'b1), .Q(out_2), .en(1'b1), .reset(and_1_out));  // open: Qn, preset
  J_K_Flip_Flop #(.trigger("falling")) j_k_ff_12 (
    .J(1'b1), .clk(out_10), .K(1'b1), .Q(out_9), .en(1'b1), .reset(and_2_out));  // open: Qn, preset
  and and_2 (and_2_out, not_3_out, not_5_out, out_10, out_9, out_8, out_7);
  J_K_Flip_Flop #(.trigger("falling")) j_k_ff_13 (
    .J(1'b1), .clk(hours), .K(1'b1), .Q(out_15), .en(1'b1), .reset(and_3_out));  // open: Qn, preset
  and and_3 (and_3_out, not_4_out, not_6_out, not_7_out, out_15, out_14, not_8_out);
  J_K_Flip_Flop #(.trigger("falling")) j_k_ff_14 (
    .J(1'b1), .clk(out_9), .K(1'b1), .Q(out_8), .en(1'b1), .reset(and_2_out));  // open: Qn, preset
  J_K_Flip_Flop #(.trigger("falling")) j_k_ff_15 (
    .J(1'b1), .clk(out_15), .K(1'b1), .Q(out_14), .en(1'b1), .reset(and_3_out));  // open: Qn, preset
  J_K_Flip_Flop #(.trigger("falling")) j_k_ff_16 (
    .J(1'b1), .clk(out_2), .K(1'b1), .Q(out_1), .en(1'b1), .reset(and_1_out));  // open: Qn, preset
  J_K_Flip_Flop #(.trigger("falling")) j_k_ff_17 (
    .J(1'b1), .clk(out_8), .K(1'b1), .Q(out_7), .en(1'b1), .reset(and_2_out));  // open: Qn, preset
  J_K_Flip_Flop #(.trigger("falling")) j_k_ff_18 (
    .J(1'b1), .clk(out_14), .K(1'b1), .Q(out_13), .en(1'b1), .reset(and_3_out));  // open: Qn, preset
  not not_8 (not_8_out, out_13);

  // Notes on the sheet:
  //   DIGITAL   CLOCK
  //   minutes
endmodule
